// Logisim project NOTGATE.circ as structural Verilog
module main (
  input  [3:0] in_a,
  output [3:0] out_y
);

  NOT_GATE n_gate (.a(in_a), .y(out_y));
endmodule

// VHDL entity NOT_GATE, as the project stores it:
LIBRARY ieee;
USE ieee.std_logic_1164.all;

ENTITY NOT_GATE IS
  PORT (
    a : IN  std_logic_vector(3 DOWNTO 0);
    y : OUT std_logic_vector(3 DOWNTO 0)
    );
END NOT_GATE;

--------------------------------------------------------------------------------
--Complete your VHDL description below
--------------------------------------------------------------------------------

ARCHITECTURE behavior OF NOT_GATE IS

BEGIN
	y <= NOT a;
	
END behavior;
