// Logisim project ANDOR_4_val.circ as structural Verilog
module main (
  input  in_1,
  input  in_2,
  input  in_3,
  input  in_4,
  output out_5,
  output out_6
);

  val_4_and_or val_4_and_or_1 (.a(in_1), .b(in_2), .c(in_3), .d(in_4), .and_out(out_5), .or_out(out_6));
endmodule

// VHDL entity val_4_and_or, as the project stores it:
LIBRARY ieee;
USE ieee.std_logic_1164.all;
USE ieee.std_logic_arith.all;
USE ieee.std_logic_unsigned.all;


--entity

ENTITY val_4_and_or IS
	PORT (
		
a,b,c,d : IN std_logic;
		and_out, or_out : OUT std_logic
	);
END ENTITY val_4_and_or;


--arcitecture
ARCHITECTURE bhv OF val_4_and_or IS

BEGIN
	and_out <= a and b and c and d;
	or_out <= a or b or c or d;


END ARCHITECTURE bhv;
