// Logisim project MULTI_8TO1.circ as structural Verilog
module main (
  input  in_1,
  input  in_2,
  input  in_3,
  input  in_4,
  input  in_5,
  input  in_6,
  input  in_7,
  input  in_8,
  input  in_9,
  input  in_10,
  input  in_11
);

  wire rgbled_1_p1;

  // RGBLED rgbled_1: pin names not known; wires that end beside it: rgbled_1_p1
  mux_8to1 mux_8to1_1 (
    .a(in_1), .b(in_2), .c(in_3), .d(in_4), .e(in_5), .f(in_6), .g(in_7), .h(in_8), .ch0(in_9), .ch1(in_10),
    .ch2(in_11), .data(rgbled_1_p1));
endmodule

// VHDL entity mux_8to1, as the project stores it:
LIBRARY ieee;
USE ieee.std_logic_1164.all;

--entity
ENTITY mux_8to1 IS
    PORT (
        a,b,c,d,e,f,g,h : IN std_logic;
        ch0,ch1,ch2     : IN std_logic;
        data : OUT std_logic
    );
END ENTITY mux_8to1;

--architecture
ARCHITECTURE bhv OF mux_8to1 IS
BEGIN
    PROCESS(a,b,c,d,e,f,g,h,ch0,ch1,ch2)
    BEGIN
        IF ch0 = '0' THEN
            IF ch1 = '0' THEN
                IF ch2 = '0' THEN
                    data <= a;   -- 000
                ELSE
                    data <= b;   -- 001
                END IF;
            ELSE
                IF ch2 = '0' THEN
                    data <= c;   -- 010
                ELSE
                    data <= d;   -- 011
                END IF;
            END IF;
        ELSE
            IF ch1 = '0' THEN
                IF ch2 = '0' THEN
                    data <= e;   -- 100
                ELSE
                    data <= f;   -- 101
                END IF;
            ELSE
                IF ch2 = '0' THEN
                    data <= g;   -- 110
                ELSE
                    data <= h;   -- 111
                END IF;
            END IF;
        END IF;
    END PROCESS;
END ARCHITECTURE bhv;
