// Logisim project SEG_7_LETTERS.circ as structural Verilog
module main (
  input  in_1,
  input  [3:0] in_2
);

  wire [7:0] dis_7seg_1_dis;

  dis_7seg dis_7seg_1 (.en(in_1), .data(in_2), .dis(dis_7seg_1_dis));
  _7_Segment_Display u_7_segment_display_1 (
    .g(dis_7seg_1_dis[1]), .f(dis_7seg_1_dis[2]), .a(dis_7seg_1_dis[7]), .b(dis_7seg_1_dis[6]),
    .e(dis_7seg_1_dis[3]), .d(dis_7seg_1_dis[4]), .c(dis_7seg_1_dis[5]), .dp(dis_7seg_1_dis[0]));
endmodule

// VHDL entity dis_7seg, as the project stores it:
LIBRARY ieee;
USE ieee.std_logic_1164.all;
USE ieee.std_logic_arith.all;
USE ieee.std_logic_unsigned.all;


--entityx
ENTITY dis_7seg IS
	PORT (
		en   : IN std_logic;
		data : IN std_logic_vector(3 DOWNTO 0);
		dis  : OUT std_logic_vector(7 DOWNTO 0)
	);
END ENTITY dis_7seg	;

--arcitecture
ARCHITECTURE bhv OF dis_7seg IS

BEGIN
	PROCESS(en,data)
	BEGIN
		IF en = '0' THEN
			dis <= "ZZZZZZZZ";
		ELSE
			CASE data IS
				WHEN "0000" => dis <= "11101110"; -- A
				WHEN "0001" => dis <= "00111110"; -- b
				WHEN "0010" => dis <= "10011100"; -- C
				WHEN "0011" => dis <= "01111010"; -- d
				WHEN "0100" => dis <= "10001110"; -- F
				WHEN "0101" => dis <= "11110110"; -- g

				WHEN others => dis <= "00000000";
			END CASE;
		END IF;
	END PROCESS;

END ARCHITECTURE bhv;
