// Logisim project VOTE15_SEG.circ as structural Verilog
module main (
  input  in_1
);

  wire [6:0] vote15_seg_1_seg;
  wire [14:0] dipswitch_1_sw15;

  DipSwitch #(.number(15)) dipswitch_1 (
    .sw1(dipswitch_1_sw15[14]), .sw2(dipswitch_1_sw15[13]), .sw3(dipswitch_1_sw15[12]),
    .sw4(dipswitch_1_sw15[11]), .sw5(dipswitch_1_sw15[10]), .sw6(dipswitch_1_sw15[9]),
    .sw7(dipswitch_1_sw15[8]), .sw8(dipswitch_1_sw15[7]), .sw9(dipswitch_1_sw15[6]),
    .sw10(dipswitch_1_sw15[5]), .sw11(dipswitch_1_sw15[4]), .sw12(dipswitch_1_sw15[3]),
    .sw13(dipswitch_1_sw15[2]), .sw14(dipswitch_1_sw15[1]), .sw15(dipswitch_1_sw15[0]));
  vote15_seg vote15_seg_1 (.vt(dipswitch_1_sw15), .en(in_1), .seg(vote15_seg_1_seg));
  _7_Segment_Display u_7_segment_display_1 (
    .g(vote15_seg_1_seg[0]), .f(vote15_seg_1_seg[1]), .a(vote15_seg_1_seg[6]), .b(vote15_seg_1_seg[5]),
    .e(vote15_seg_1_seg[2]), .d(vote15_seg_1_seg[3]), .c(vote15_seg_1_seg[4]));  // open: dp
endmodule

// VHDL entity vote15_seg, as the project stores it:
LIBRARY ieee;
USE ieee.std_logic_1164.all;
USE ieee.std_logic_arith.all;
USE ieee.std_logic_unsigned.all;

--entity
ENTITY vote15_seg IS
	PORT (
        	vt  : IN  std_logic_vector(14 DOWNTO 0);  
        	en  : IN  std_logic;                   
       	seg : OUT std_logic_vector(6 DOWNTO 0)
     );
END ENTITY vote15_seg;

--architecture
ARCHITECTURE bhv OF vote15_seg IS
BEGIN
    PROCESS(vt, en)
        VARIABLE cnt : integer RANGE 0 TO 15;
    BEGIN
        cnt := 0;
        FOR i IN vt'RANGE LOOP
            IF vt(i) = '1' THEN
                cnt := cnt + 1;
            END IF;
        END LOOP;

        IF en = '0' THEN
            seg <= "0000000";
        ELSE
            CASE cnt IS
                WHEN 0  => seg <= "1111110"; -- 0
                WHEN 1  => seg <= "0110000"; -- 1
                WHEN 2  => seg <= "1101101"; -- 2
                WHEN 3  => seg <= "1111001"; -- 3
                WHEN 4  => seg <= "0110011"; -- 4
                WHEN 5  => seg <= "1011011"; -- 5
                WHEN 6  => seg <= "1011111"; -- 6
                WHEN 7  => seg <= "1110000"; -- 7
                WHEN 8  => seg <= "1111111"; -- 8
                WHEN 9  => seg <= "1111011"; -- 9
                WHEN 10 => seg <= "1110111"; -- A
           	 WHEN 11 => seg <= "0011111"; -- b
                WHEN 12 => seg <= "1001110"; -- C
                WHEN 13 => seg <= "0111101"; -- d
                WHEN 14 => seg <= "1001111"; -- E
                WHEN 15 => seg <= "1000111"; -- F
                WHEN OTHERS => seg <= "0000000";
            END CASE;
        END IF;
    END PROCESS;
    
END ARCHITECTURE bhv;
