// Logisim project VOTING_25.circ as structural Verilog
module main (
);

  wire vote25_1_res;
  wire [24:0] dipswitch_1_sw25;

  DipSwitch #(.number(25)) dipswitch_1 (
    .sw1(dipswitch_1_sw25[24]), .sw2(dipswitch_1_sw25[23]), .sw3(dipswitch_1_sw25[22]),
    .sw4(dipswitch_1_sw25[21]), .sw5(dipswitch_1_sw25[20]), .sw6(dipswitch_1_sw25[19]),
    .sw7(dipswitch_1_sw25[18]), .sw8(dipswitch_1_sw25[17]), .sw9(dipswitch_1_sw25[16]),
    .sw10(dipswitch_1_sw25[15]), .sw11(dipswitch_1_sw25[14]), .sw12(dipswitch_1_sw25[13]),
    .sw13(dipswitch_1_sw25[12]), .sw14(dipswitch_1_sw25[11]), .sw15(dipswitch_1_sw25[10]),
    .sw16(dipswitch_1_sw25[9]), .sw17(dipswitch_1_sw25[8]), .sw18(dipswitch_1_sw25[7]),
    .sw19(dipswitch_1_sw25[6]), .sw20(dipswitch_1_sw25[5]), .sw21(dipswitch_1_sw25[4]),
    .sw22(dipswitch_1_sw25[3]), .sw23(dipswitch_1_sw25[2]), .sw24(dipswitch_1_sw25[1]),
    .sw25(dipswitch_1_sw25[0]));
  vote25 vote25_1 (.vt(dipswitch_1_sw25), .res(vote25_1_res));
  LED led_1 (.in(vote25_1_res));
endmodule

// VHDL entity vote25, as the project stores it:
LIBRARY ieee;
USE ieee.std_logic_1164.all;
USE ieee.std_logic_arith.all;
USE ieee.std_logic_unsigned.all;


--entityx
ENTITY vote25 IS
	PORT (
		vt : IN std_logic_vector(25 DOWNTO 1);
		res : OUT std_logic
	);
END ENTITY vote25;

--arcitecture
ARCHITECTURE bhv OF vote25 IS

BEGIN
	PROCESS(vt)
	VARIABLE sum : integer RANGE 0 TO 25;
	BEGIN
		sum := 0;
		FOR i IN 1 TO 25 LOOP
			IF (vt(i) = '1') THEN
				sum := sum+1;
				IF sum >= 13 THEN
					res <= '1';
				ELSE
					res <= '0';
				END IF;
			END IF;
		END LOOP;
	END PROCESS;

END ARCHITECTURE bhv;
