// Logisim project 3+5. D_FlipFlop & D_FlipFlop_clr_set_CIRC.circ as structural Verilog
module main (
  input  D,
  input  CLK,
  input  in_3,
  input  in_4,
  input  in_5,
  input  in_6,
  input  in_7,
  input  in_8,
  input  in_9,
  input  in_10,
  output Q,
  output out_12,
  output NOT_Q,
  output out_14,
  output out_15,
  output out_16,
  output out_17
);

  wire nand_1_out, nand_2_out, nand_3_out, nand_5_out, nand_6_out, not_1_out, not_2_out, not_3_out;

  not not_1 (not_1_out, CLK);
  not not_2 (not_2_out, D);
  D_Flip_Flop d_ff_1 (.D(in_3), .clk(in_6), .Q(out_14), .Qn(out_16));  // open: preset, reset
  nand nand_1 (nand_1_out, D, not_1_out);
  nand nand_2 (nand_2_out, not_1_out, not_2_out);
  nand nand_3 (nand_3_out, nand_1_out, out_12);
  nand nand_4 (out_12, nand_3_out, nand_2_out);
  nand nand_5 (nand_5_out, nand_3_out, CLK);
  nand nand_6 (nand_6_out, CLK, not_3_out);
  not not_3 (not_3_out, nand_3_out);
  nand nand_7 (Q, nand_5_out, NOT_Q);
  nand nand_8 (NOT_Q, Q, nand_6_out);
  D_FlipFlop d_flipflop_1 (.clk(in_4), .D(in_5), .Q(out_15));
  D_FlipFlop_clr_set d_flipflop_clr_set_1 (.clk(in_7), .clr(in_8), .set(in_9), .D(in_10), .Q(out_17));

  // Notes on the sheet:
  //   D_FLIP-FLOP
  //   VHDL_CIRC
endmodule

// VHDL entity D_FlipFlop, as the project stores it:
LIBRARY ieee;
USE ieee.std_logic_1164.ALL;

ENTITY D_FlipFlop IS
PORT (
	clk : IN std_logic;
	D   : IN std_logic;
	Q   : OUT std_logic
);
END D_FlipFlop;


ARCHITECTURE bhv OF D_FlipFlop IS

BEGIN

	PROCESS(clk)
	BEGIN
		IF (clk'event AND clk = '1') THEN
			Q <= D;

		END IF;
		
	END PROCESS;
END bhv;

// VHDL entity D_FlipFlop_clr_set, as the project stores it:
LIBRARY ieee;
USE ieee.std_logic_1164.ALL;

ENTITY D_FlipFlop_clr_set IS
PORT (
	clk : IN std_logic;
	clr : IN std_logic;
	set : IN std_logic;
	D   : IN std_logic;
	Q   : OUT std_logic
);
END D_FlipFlop_clr_set;


ARCHITECTURE bhv OF D_FlipFlop_clr_set IS

BEGIN

	PROCESS(clk,clr,set)
	BEGIN
		IF clr = '1' THEN
			Q <= '0';
		ELSIF set = '1' THEN
			Q <= '1';
		ELSIF (clk'event AND clk = '1') THEN
			Q <= D;

		END IF;
		
	END PROCESS;
END bhv;
