// Logisim project 4. JK_FlipFlop_CIRC.circ as structural Verilog
module main (
  input  J,
  input  CLK,
  input  K,
  input  EN,
  input  in_5,
  input  in_6,
  input  in_7,
  input  in_8,
  input  in_9,
  input  in_10,
  input  in_11,
  input  in_12,
  input  in_13,
  input  in_14,
  output Q,
  output not_Q,
  output out_17,
  output out_18,
  output out_19
);

  wire nand_1_out, nand_2_out, nand_3_out, nand_4_out, nand_5_out, nand_6_out, not_1_out;

  not not_1 (not_1_out, CLK);
  J_K_Flip_Flop j_k_ff_1 (.J(in_8), .K(in_10), .clk(in_12), .Q(out_18), .Qn(out_19), .preset(in_6), .reset(in_14));
  nand nand_1 (nand_1_out, not_Q, J, not_1_out);
  nand nand_2 (nand_2_out, not_1_out, K, Q);
  nand nand_3 (nand_3_out, nand_1_out, nand_4_out);
  nand nand_4 (nand_4_out, nand_3_out, EN, nand_2_out);
  nand nand_5 (nand_5_out, nand_3_out, CLK);
  nand nand_6 (nand_6_out, CLK, nand_4_out);
  nand nand_7 (Q, nand_5_out, not_Q);
  nand nand_8 (not_Q, Q, EN, nand_6_out);
  JK_FlipFlop jk_flipflop_1 (.clr(in_5), .set(in_7), .clk(in_9), .J(in_11), .K(in_13), .Q(out_17));
endmodule

// VHDL entity JK_FlipFlop, as the project stores it:
LIBRARY ieee;
USE ieee.std_logic_1164.ALL;
USE ieee.numeric_std.ALL;

ENTITY JK_FlipFlop IS
PORT (
	clr : IN std_logic;
	set : IN std_logic;
	clk : IN std_logic;
	J   : IN std_logic;
	K   : IN std_logic;
	Q   : OUT std_logic
);
END JK_FlipFlop;


ARCHITECTURE bhv OF JK_FlipFlop IS
SIGNAL Q_temp : std_logic := '0';

BEGIN
	Q <= Q_temp;
	PROCESS(clk,clr,set)
	BEGIN
		IF clr = '1' THEN   -- CLEAR (RESET)
			Q_temp <= '0';
		ELSIF set = '1' THEN   -- SET
			Q_temp <= '1';
			
		ELSIF (clk'event AND clk = '1') THEN
			IF (J = '1' AND K = '0') THEN    -- SET
				Q_temp <= '1';
			ELSIF (J = '0' AND K = '1') THEN -- RESET
				Q_temp <= '0';
			ELSIF (J = '1' AND K = '1') THEN -- TOGLE
				Q_temp <= NOT Q_temp;
					
			END IF;
		
	END PROCESS;
END ARCHITECTURE bhv;
