// Logisim project SR_latch & D_latch_CIRC.circ as structural Verilog
module main (
  input  S_1,
  input  R_1,
  input  R_2,
  input  S_2,
  input  D,
  input  EN,
  input  in_7,
  input  in_8,
  input  in_9,
  input  in_10,
  output Q_1,
  output not_Q_1,
  output Q_2,
  output not_Q_2,
  output Q3,
  output not_Q_3,
  output out_17,
  output out_18
);

  wire nand_3_out, nand_4_out, not_1_out;

  nand nand_1 (Q_1, S_1, not_Q_1);
  nand nand_2 (not_Q_1, Q_1, R_1);
  nor nor_1 (Q_2, R_2, not_Q_2);
  nor nor_2 (not_Q_2, Q_2, S_2);
  not not_1 (not_1_out, D);
  nand nand_3 (nand_3_out, D, EN);
  nand nand_4 (nand_4_out, EN, not_1_out);
  SR_latch sr_latch_1 (.S(in_7), .R(in_8), .Q(out_17));
  D_Latch d_latch_1 (.en(in_9), .D(in_10), .Q(out_18));
  nand nand_5 (Q3, nand_3_out, not_Q_3);
  nand nand_6 (not_Q_3, Q3, nand_4_out);

  // Notes on the sheet:
  //   SR_LATCH (NOR & NAND)
  //   D_LATCH
  //   VHDL_CIRC
endmodule

// VHDL entity D_Latch, as the project stores it:
LIBRARY ieee;
USE ieee.std_logic_1164.ALL;

ENTITY D_Latch IS
PORT (
	en : IN std_logic;
	D   : IN std_logic;
	Q   : OUT std_logic
);
END D_Latch;

ARCHITECTURE bhv OF D_Latch IS
BEGIN

	PROCESS(en,D)
	BEGIN
		IF (en = '1') THEN
			Q <= D;

		END IF;
		
	END PROCESS;
END bhv;

// VHDL entity SR_latch, as the project stores it:
LIBRARY IEEE;
USE IEEE.STD_LOGIC_1164.ALL;
USE ieee.numeric_std.ALL;

ENTITY SR_latch IS
PORT ( 
	S,R : IN    STD_LOGIC;
     Q   : OUT   STD_LOGIC
);
END SR_latch;

ARCHITECTURE bhv OF SR_latch IS
SIGNAL notQ : STD_LOGIC;
SIGNAL Q_temp : STD_LOGIC;
BEGIN

Q   <= Q_temp;
Q_temp  <= R nor notQ;
notQ <= S nor Q_temp;
end bhv;
